# Fritzing sketch alat rivan (saved by Fritzing 0.9.3b)

parts:
  U1 = ESP8266 NodeMCU LoLin base
  BAT2 = Battery Holders [package=battery-aa-panel]
  BAT1 = Battery Holders [package=battery-aa-panel]
  RY1 = KF-301 Relay [package=THT]
  L1 = Solenoid
  BAT3 = Battery Holders [package=battery-aa-panel]
  Part1 = RFID-RC522-v2

nets:
  N1: U1.D0-0, U1.D0-3, RY1.signal
  N2: U1.D3-0, U1.D3-3, Part1.RST
  N3: U1.D4-0, Part1.SDA
  N4: U1.3V2-0, U1.3V3-0, U1.3V3-2, RY1.power, Part1.3.3V
  GND6: U1.GND2-0, U1.GND3-0, U1.GND3-2, U1.GND6, RY1.ground, Part1.GND
  N5: U1.D5-0, Part1.SCK
  N6: U1.D6-0, Part1.MISO
  N7: U1.D7-0, Part1.MOSI
  N8: BAT2.+, BAT3.-
  N9: BAT2.-, BAT1.+
  N10: BAT1.-, L1.pin1
  N11: RY1.C, L1.pin2
  N12: RY1.NO, BAT3.+

custom parts:
  ESP8266 NodeMCU LoLin base: ESP8266 based NodeMCU Base
  KF-301 Relay: KF-301 SPDT Relay module using SRD-05VDC-SL-C relay.
  RFID-RC522-v2: A simple China made RFID-RC522 Reader; do check the pin labels, as this is a MFRC522 based clone.
